# Fritzing sketch photon_flash_trigger (saved by Fritzing 0.9.2b)
circuit board: 4.71879cm x 2.83866cm
breadboards: 1

parts:
  Photon = Photon
  MOC3021 = MOC3031-M [package=dil06]
  LDR = Photocell (LDR) [package=THT]
  1K = Resistor [tolerance=±5% resistance=220 package=THT]

nets:
  N1: Photon.A0, LDR.pin_0, 1K.Pin_0
  N2: Photon.A3, LDR.pin_1
  N3: Photon.GND, MOC3021.2, 1K.Pin_1
  N4: Photon.D1, MOC3021.1

notes:
  Flash pin
